// Logisim project trab.circ as structural Verilog: 13 circuits, main circuit main
module main (
  output [31:0] Display,
  output [31:0] out_2,
  output [31:0] out_3,
  output [31:0] out_4,
  output [3:0] out_5,
  output [2:0] out_6,
  output [3:0] out_7,
  output [31:0] out_8,
  output out_9,
  output [3:0] out_10,
  output out_11,
  output [3:0] out_12,
  output out_13,
  output out_14
);

  wire and_1_out, clk, reset_out, ZeroULA;
  wire [15:0] imm16;
  wire [31:0] BancoDeReg_b, imm32, multiplexer_1_out, somador_1_ssoma, somador_2_ssoma;

  Clock clock_1 (.out(clk));
  somador somador_1 (.A(32'h1), .B(out_2), .sSoma(somador_1_ssoma));
  and and_1 (and_1_out, out_14, ZeroULA);
  Multiplexer #(.width(32)) multiplexer_1 (
    .in0(somador_1_ssoma), .in1(somador_2_ssoma), .out(multiplexer_1_out), .sel(and_1_out));
  Button reset (.out(reset_out));
  somador somador_2 (.A(imm32), .B(out_2), .sSoma(somador_2_ssoma));
  reg32bits reg32bits_1 (.Dx(multiplexer_1_out), .w(1'b1), .clk(clk), .reset(reset_out), .Rx(out_2));
  ROM #(.addrWidth(24), .dataWidth(32)) MemDeInstrucao (
    .addr(out_2[23:0]), .data({out_5, out_7, out_10, out_12, imm16}));
  // NoConnect on out_2[31:24]
  br16x32 BancoDeReg (
    .C(out_8), .clk(clk), .W(out_11), .SelW(out_12), .SelR1(out_7), .SelR2(out_10), .A(out_3),
    .B(BancoDeReg_b));
  extensinal extensinal_1 (.E(imm16), .out_2(imm32));
  Multiplexer #(.width(32)) multiplexer_2 (.in0({32{1'b0}}), .in1(out_3), .out(Display), .sel(out_13));
  Multiplexer #(.width(32)) multiplexer_3 (.in0(BancoDeReg_b), .in1(imm32), .out(out_4), .sel(out_9));
  ROM #(.addrWidth(4), .dataWidth(7)) MemDeControle (.addr(out_5), .data({out_6, out_9, out_11, out_13, out_14}));
  Ula ula_1 (.A(out_3), .B(out_4), .Seletor(out_6), .S0(ZeroULA), .R(out_8));

  // Other names for the same wires on the sheet: c[3:0] = out_12; b_t[3:0] = out_10; a_t[3:0] = out_7;
  //   opCode[3:0] = out_5; PCSrc = out_14; enDisplay = out_13; WriteRG = out_11; ULASrc = out_9; ULAOp[2:0] = out_6;
  //   A[31:0] = out_3; B[31:0] = out_4; SaidaPC[31:0] = out_2; SaidaULA[31:0] = out_8

  // Notes on the sheet:
  //   Processador
  //   PC+1
  //   Debug
  //   Pc
  //   branch:PC+imm
  //   contents of MemDeInstrucao (hex, n*v repeats v):
  //   0 9001000a 90020000 90030007 90040012 90050000 c2100007 42460000 26360000 25650000 d5000000 92020001
  //   b000fffa d5000000 e0000000
  //   enableDisplay
  //   ULASrc
  //   contents of MemDeControle (hex, n*v repeats v):
  //   0 c 4 14 24 34 44 54 64 c 1c 11 11 2 9
endmodule

module reg32bits (
  input  [31:0] Dx,
  input  w,
  input  clk,
  input  reset,
  output [31:0] Rx
);

  wire multiplexer_1_out, multiplexer_2_out, multiplexer_3_out, multiplexer_4_out, multiplexer_5_out,
       multiplexer_6_out, multiplexer_7_out, multiplexer_8_out, multiplexer_9_out, multiplexer_10_out,
       multiplexer_11_out, multiplexer_12_out, multiplexer_13_out, multiplexer_14_out, multiplexer_15_out,
       multiplexer_16_out, multiplexer_17_out, multiplexer_18_out, multiplexer_19_out, multiplexer_20_out,
       multiplexer_21_out, multiplexer_22_out, multiplexer_23_out, multiplexer_24_out, multiplexer_25_out,
       multiplexer_26_out, multiplexer_27_out, multiplexer_28_out, multiplexer_29_out, multiplexer_30_out,
       multiplexer_31_out, multiplexer_32_out;

  Multiplexer multiplexer_1 (.in0(Rx[4]), .in1(Dx[4]), .out(multiplexer_1_out), .sel(w));
  Multiplexer multiplexer_2 (.in0(Rx[8]), .in1(Dx[8]), .out(multiplexer_2_out), .sel(w));
  Multiplexer multiplexer_3 (.in0(Rx[12]), .in1(Dx[12]), .out(multiplexer_3_out), .sel(w));
  Multiplexer multiplexer_4 (.in0(Rx[16]), .in1(Dx[16]), .out(multiplexer_4_out), .sel(w));
  D_Flip_Flop d_ff_1 (.D(multiplexer_5_out), .clk(clk), .Q(Rx[0]), .reset(reset));  // open: Qn, preset
  Multiplexer multiplexer_5 (.in0(Rx[0]), .in1(Dx[0]), .out(multiplexer_5_out), .sel(w));
  D_Flip_Flop d_ff_2 (.D(multiplexer_1_out), .clk(clk), .Q(Rx[4]), .reset(reset));  // open: Qn, preset
  D_Flip_Flop d_ff_3 (.D(multiplexer_2_out), .clk(clk), .Q(Rx[8]), .reset(reset));  // open: Qn, preset
  D_Flip_Flop d_ff_4 (.D(multiplexer_3_out), .clk(clk), .Q(Rx[12]), .reset(reset));  // open: Qn, preset
  D_Flip_Flop d_ff_5 (.D(multiplexer_4_out), .clk(clk), .Q(Rx[16]), .reset(reset));  // open: Qn, preset
  D_Flip_Flop d_ff_6 (.D(multiplexer_6_out), .clk(clk), .Q(Rx[20]), .reset(reset));  // open: Qn, preset
  Multiplexer multiplexer_6 (.in0(Rx[20]), .in1(Dx[20]), .out(multiplexer_6_out), .sel(w));
  D_Flip_Flop d_ff_7 (.D(multiplexer_7_out), .clk(clk), .Q(Rx[24]), .reset(reset));  // open: Qn, preset
  Multiplexer multiplexer_7 (.in0(Rx[24]), .in1(Dx[24]), .out(multiplexer_7_out), .sel(w));
  D_Flip_Flop d_ff_8 (.D(multiplexer_8_out), .clk(clk), .Q(Rx[28]), .reset(reset));  // open: Qn, preset
  Multiplexer multiplexer_8 (.in0(Rx[28]), .in1(Dx[28]), .out(multiplexer_8_out), .sel(w));
  D_Flip_Flop d_ff_9 (.D(multiplexer_9_out), .clk(clk), .Q(Rx[1]), .reset(reset));  // open: Qn, preset
  Multiplexer multiplexer_9 (.in0(Rx[1]), .in1(Dx[1]), .out(multiplexer_9_out), .sel(w));
  D_Flip_Flop d_ff_10 (.D(multiplexer_10_out), .clk(clk), .Q(Rx[5]), .reset(reset));  // open: Qn, preset
  Multiplexer multiplexer_10 (.in0(Rx[5]), .in1(Dx[5]), .out(multiplexer_10_out), .sel(w));
  D_Flip_Flop d_ff_11 (.D(multiplexer_11_out), .clk(clk), .Q(Rx[9]), .reset(reset));  // open: Qn, preset
  Multiplexer multiplexer_11 (.in0(Rx[9]), .in1(Dx[9]), .out(multiplexer_11_out), .sel(w));
  D_Flip_Flop d_ff_12 (.D(multiplexer_12_out), .clk(clk), .Q(Rx[13]), .reset(reset));  // open: Qn, preset
  Multiplexer multiplexer_12 (.in0(Rx[13]), .in1(Dx[13]), .out(multiplexer_12_out), .sel(w));
  D_Flip_Flop d_ff_13 (.D(multiplexer_13_out), .clk(clk), .Q(Rx[17]), .reset(reset));  // open: Qn, preset
  Multiplexer multiplexer_13 (.in0(Rx[17]), .in1(Dx[17]), .out(multiplexer_13_out), .sel(w));
  D_Flip_Flop d_ff_14 (.D(multiplexer_14_out), .clk(clk), .Q(Rx[21]), .reset(reset));  // open: Qn, preset
  Multiplexer multiplexer_14 (.in0(Rx[21]), .in1(Dx[21]), .out(multiplexer_14_out), .sel(w));
  D_Flip_Flop d_ff_15 (.D(multiplexer_15_out), .clk(clk), .Q(Rx[25]), .reset(reset));  // open: Qn, preset
  Multiplexer multiplexer_15 (.in0(Rx[25]), .in1(Dx[25]), .out(multiplexer_15_out), .sel(w));
  D_Flip_Flop d_ff_16 (.D(multiplexer_16_out), .clk(clk), .Q(Rx[29]), .reset(reset));  // open: Qn, preset
  Multiplexer multiplexer_16 (.in0(Rx[29]), .in1(Dx[29]), .out(multiplexer_16_out), .sel(w));
  D_Flip_Flop d_ff_17 (.D(multiplexer_17_out), .clk(clk), .Q(Rx[2]), .reset(reset));  // open: Qn, preset
  Multiplexer multiplexer_17 (.in0(Rx[2]), .in1(Dx[2]), .out(multiplexer_17_out), .sel(w));
  D_Flip_Flop d_ff_18 (.D(multiplexer_18_out), .clk(clk), .Q(Rx[6]), .reset(reset));  // open: Qn, preset
  Multiplexer multiplexer_18 (.in0(Rx[6]), .in1(Dx[6]), .out(multiplexer_18_out), .sel(w));
  D_Flip_Flop d_ff_19 (.D(multiplexer_19_out), .clk(clk), .Q(Rx[10]), .reset(reset));  // open: Qn, preset
  Multiplexer multiplexer_19 (.in0(Rx[10]), .in1(Dx[10]), .out(multiplexer_19_out), .sel(w));
  D_Flip_Flop d_ff_20 (.D(multiplexer_20_out), .clk(clk), .Q(Rx[14]), .reset(reset));  // open: Qn, preset
  Multiplexer multiplexer_20 (.in0(Rx[14]), .in1(Dx[14]), .out(multiplexer_20_out), .sel(w));
  D_Flip_Flop d_ff_21 (.D(multiplexer_21_out), .clk(clk), .Q(Rx[18]), .reset(reset));  // open: Qn, preset
  Multiplexer multiplexer_21 (.in0(Rx[18]), .in1(Dx[18]), .out(multiplexer_21_out), .sel(w));
  D_Flip_Flop d_ff_22 (.D(multiplexer_22_out), .clk(clk), .Q(Rx[22]), .reset(reset));  // open: Qn, preset
  Multiplexer multiplexer_22 (.in0(Rx[22]), .in1(Dx[22]), .out(multiplexer_22_out), .sel(w));
  D_Flip_Flop d_ff_23 (.D(multiplexer_23_out), .clk(clk), .Q(Rx[26]), .reset(reset));  // open: Qn, preset
  Multiplexer multiplexer_23 (.in0(Rx[26]), .in1(Dx[26]), .out(multiplexer_23_out), .sel(w));
  D_Flip_Flop d_ff_24 (.D(multiplexer_24_out), .clk(clk), .Q(Rx[30]), .reset(reset));  // open: Qn, preset
  Multiplexer multiplexer_24 (.in0(Rx[30]), .in1(Dx[30]), .out(multiplexer_24_out), .sel(w));
  D_Flip_Flop d_ff_25 (.D(multiplexer_25_out), .clk(clk), .Q(Rx[3]), .reset(reset));  // open: Qn, preset
  Multiplexer multiplexer_25 (.in0(Rx[3]), .in1(Dx[3]), .out(multiplexer_25_out), .sel(w));
  D_Flip_Flop d_ff_26 (.D(multiplexer_26_out), .clk(clk), .Q(Rx[7]), .reset(reset));  // open: Qn, preset
  Multiplexer multiplexer_26 (.in0(Rx[7]), .in1(Dx[7]), .out(multiplexer_26_out), .sel(w));
  D_Flip_Flop d_ff_27 (.D(multiplexer_27_out), .clk(clk), .Q(Rx[11]), .reset(reset));  // open: Qn, preset
  Multiplexer multiplexer_27 (.in0(Rx[11]), .in1(Dx[11]), .out(multiplexer_27_out), .sel(w));
  D_Flip_Flop d_ff_28 (.D(multiplexer_28_out), .clk(clk), .Q(Rx[15]), .reset(reset));  // open: Qn, preset
  Multiplexer multiplexer_28 (.in0(Rx[15]), .in1(Dx[15]), .out(multiplexer_28_out), .sel(w));
  D_Flip_Flop d_ff_29 (.D(multiplexer_29_out), .clk(clk), .Q(Rx[19]), .reset(reset));  // open: Qn, preset
  Multiplexer multiplexer_29 (.in0(Rx[19]), .in1(Dx[19]), .out(multiplexer_29_out), .sel(w));
  D_Flip_Flop d_ff_30 (.D(multiplexer_30_out), .clk(clk), .Q(Rx[23]), .reset(reset));  // open: Qn, preset
  Multiplexer multiplexer_30 (.in0(Rx[23]), .in1(Dx[23]), .out(multiplexer_30_out), .sel(w));
  D_Flip_Flop d_ff_31 (.D(multiplexer_31_out), .clk(clk), .Q(Rx[27]), .reset(reset));  // open: Qn, preset
  Multiplexer multiplexer_31 (.in0(Rx[27]), .in1(Dx[27]), .out(multiplexer_31_out), .sel(w));
  D_Flip_Flop d_ff_32 (.D(multiplexer_32_out), .clk(clk), .Q(Rx[31]), .reset(reset));  // open: Qn, preset
  Multiplexer multiplexer_32 (.in0(Rx[31]), .in1(Dx[31]), .out(multiplexer_32_out), .sel(w));

  // Other names for the same wires on the sheet: dx00 = Dx[0]; dx01 = Dx[1]; dx02 = Dx[2]; dx03 = Dx[3]; dx04 = Dx[4];
  //   dx05 = Dx[5]; dx06 = Dx[6]; dx07 = Dx[7]; dx08 = Dx[8]; dx09 = Dx[9]; qx00 = Rx[0]; qx01 = Rx[1]; qx02 = Rx[2];
  //   qx03 = Rx[3]; qx04 = Rx[4]; qx05 = Rx[5]; qx06 = Rx[6]; qx07 = Rx[7]; qx08 = Rx[8]; qx09 = Rx[9]; qx10 = Rx[10];
  //   qx11 = Rx[11]; qx12 = Rx[12]; qx13 = Rx[13]; qx14 = Rx[14]; qx15 = Rx[15]; qx16 = Rx[16]; qx17 = Rx[17];
  //   qx18 = Rx[18]; qx19 = Rx[19]; qx20 = Rx[20]; qx21 = Rx[21]; qx22 = Rx[22]; qx23 = Rx[23]; qx24 = Rx[24];
  //   qx25 = Rx[25]; qx26 = Rx[26]; qx27 = Rx[27]; qx28 = Rx[28]; qx29 = Rx[29]; qx30 = Rx[30]; qx31 = Rx[31]
endmodule

module br16x32 (
  input  [31:0] C,
  input  clk,
  input  W,
  input  [3:0] SelW,
  input  [3:0] SelR1,
  input  [3:0] SelR2,
  output [31:0] A,
  output [31:0] B
);

  wire demultiplexer_1_out0, undriven_2, undriven_3, undriven_4, undriven_5, undriven_6, undriven_7,
       undriven_8, undriven_9, undriven_10, undriven_11, undriven_12, undriven_13, undriven_14, undriven_15,
       undriven_16, undriven_17, undriven_18, w1, w2, w3, w4, w5, w6, w7, w8, w9, w10, w11, w12, w13, w14,
       w15;
  wire [31:0] e00, e01, e02, e03, e04, e05, e06, e07, e08, e09, e10, e11, e12, e13, e14, e15, undriven;

  // NoConnect on demultiplexer_1_out0
  Demultiplexer #(.select(4)) demultiplexer_1 (
    .out0(demultiplexer_1_out0), .out1(w1), .out2(w2), .out3(w3), .out4(w4), .out5(w5), .out6(w6), .out7(w7),
    .out8(w8), .out9(w9), .out10(w10), .out11(w11), .out12(w12), .out13(w13), .out14(w14), .out15(w15),
    .in(W), .sel(SelW));
  Multiplexer #(.select(4), .width(32)) multiplexer_1 (
    .in0(e00), .in1(e01), .in2(e02), .in3(e03), .in4(e04), .in5(e05), .in6(e06), .in7(e07), .in8(e08),
    .in9(e09), .in10(e10), .in11(e11), .in12(e12), .in13(e13), .in14(e14), .in15(e15), .out(A), .sel(SelR1));
  Multiplexer #(.select(4), .width(32)) multiplexer_2 (
    .in0(e00), .in1(e01), .in2(e02), .in3(e03), .in4(e04), .in5(e05), .in6(e06), .in7(e07), .in8(e08),
    .in9(e09), .in10(e10), .in11(e11), .in12(e12), .in13(e13), .in14(e14), .in15(e15), .out(B), .sel(SelR2));
  // NoConnect on undriven
  // NoConnect on undriven_2
  // NoConnect on undriven_3
  // NoConnect on undriven_4
  // NoConnect on undriven_5
  // NoConnect on undriven_6
  reg32bits reg32bits_1 (.Dx(undriven), .w(undriven_2), .clk(clk), .reset(undriven_3), .Rx(e00));
  reg32bits reg32bits_2 (.Dx(C), .w(w1), .clk(clk), .reset(undriven_4), .Rx(e01));
  reg32bits reg32bits_3 (.Dx(C), .w(w2), .clk(clk), .reset(undriven_5), .Rx(e02));
  reg32bits reg32bits_4 (.Dx(C), .w(w3), .clk(clk), .reset(undriven_6), .Rx(e03));
  // NoConnect on undriven_7
  // NoConnect on undriven_8
  // NoConnect on undriven_9
  // NoConnect on undriven_10
  reg32bits reg32bits_5 (.Dx(C), .w(w4), .clk(clk), .reset(undriven_7), .Rx(e04));
  reg32bits reg32bits_6 (.Dx(C), .w(w5), .clk(clk), .reset(undriven_8), .Rx(e05));
  reg32bits reg32bits_7 (.Dx(C), .w(w6), .clk(clk), .reset(undriven_9), .Rx(e06));
  reg32bits reg32bits_8 (.Dx(C), .w(w7), .clk(clk), .reset(undriven_10), .Rx(e07));
  // NoConnect on undriven_11
  // NoConnect on undriven_12
  // NoConnect on undriven_13
  // NoConnect on undriven_14
  reg32bits reg32bits_9 (.Dx(C), .w(w8), .clk(clk), .reset(undriven_11), .Rx(e08));
  reg32bits reg32bits_10 (.Dx(C), .w(w9), .clk(clk), .reset(undriven_12), .Rx(e09));
  reg32bits reg32bits_11 (.Dx(C), .w(w10), .clk(clk), .reset(undriven_13), .Rx(e10));
  reg32bits reg32bits_12 (.Dx(C), .w(w11), .clk(clk), .reset(undriven_14), .Rx(e11));
  // NoConnect on undriven_15
  // NoConnect on undriven_16
  // NoConnect on undriven_17
  // NoConnect on undriven_18
  reg32bits reg32bits_13 (.Dx(C), .w(w12), .clk(clk), .reset(undriven_15), .Rx(e12));
  reg32bits reg32bits_14 (.Dx(C), .w(w13), .clk(clk), .reset(undriven_16), .Rx(e13));
  reg32bits reg32bits_15 (.Dx(C), .w(w14), .clk(clk), .reset(undriven_17), .Rx(e14));
  reg32bits reg32bits_16 (.Dx(C), .w(w15), .clk(clk), .reset(undriven_18), .Rx(e15));

  // Notes on the sheet:
  //   leitura1
  //   leitura2
endmodule

module Ula (
  input  [31:0] A,
  input  [31:0] B,
  input  [2:0] Seletor,
  output S0,
  output [31:0] R
);

  wire not_1_out, not_2_out, not_3_out, not_4_out, not_5_out, not_6_out, not_7_out, not_8_out, not_9_out,
       not_10_out, not_11_out, not_12_out, not_13_out, not_14_out, not_15_out, not_16_out, not_17_out,
       not_18_out, not_19_out, not_20_out, not_21_out, not_22_out, not_23_out, not_24_out, not_25_out,
       not_26_out, not_27_out, not_28_out, not_29_out, not_30_out, not_31_out, not_32_out;
  wire [31:0] R0, R1, R2, R3, R4, R5, R6;

  Multiplexer #(.select(3), .width(32)) multiplexer_1 (
    .in0(R0), .in1(R1), .in2(R2), .in3(R3), .in4(R4), .in5(R5), .in6(R6), .in7({32{1'b0}}), .out(R),
    .sel(Seletor));
  somador somador_1 (.A(A), .B(B), .sSoma(R0));
  subtrator subtrator_1 (.A(A), .B(B), .sSub(R1));
  multiplicador multiplicador_1 (.A(A), .B(B), .sMult(R2));
  ulaAND ulaand_1 (.A(A), .B(B), .sAND(R3));
  ulaOR ulaor_1 (.A(A), .B(B), .sOR(R4));
  ulaXOR ulaxor_1 (.A(A), .B(B), .sXOR(R5));
  deslocEsq deslocesq_1 (.A(A), .B(B), .sDesl(R6));
  not not_1 (not_1_out, R[0]);
  not not_2 (not_2_out, R[1]);
  not not_3 (not_3_out, R[2]);
  not not_4 (not_4_out, R[3]);
  not not_5 (not_5_out, R[4]);
  not not_6 (not_6_out, R[5]);
  not not_7 (not_7_out, R[6]);
  not not_8 (not_8_out, R[7]);
  not not_9 (not_9_out, R[8]);
  not not_10 (not_10_out, R[9]);
  not not_11 (not_11_out, R[10]);
  not not_12 (not_12_out, R[11]);
  not not_13 (not_13_out, R[12]);
  not not_14 (not_14_out, R[13]);
  not not_15 (not_15_out, R[14]);
  not not_16 (not_16_out, R[15]);
  not not_17 (not_17_out, R[16]);
  not not_18 (not_18_out, R[17]);
  not not_19 (not_19_out, R[18]);
  not not_20 (not_20_out, R[19]);
  not not_21 (not_21_out, R[20]);
  not not_22 (not_22_out, R[21]);
  not not_23 (not_23_out, R[22]);
  not not_24 (not_24_out, R[23]);
  not not_25 (not_25_out, R[24]);
  not not_26 (not_26_out, R[25]);
  not not_27 (not_27_out, R[26]);
  not not_28 (not_28_out, R[27]);
  not not_29 (not_29_out, R[28]);
  not not_30 (not_30_out, R[29]);
  not not_31 (not_31_out, R[30]);
  not not_32 (not_32_out, R[31]);
  and and_1 (S0, not_1_out, not_2_out, not_3_out, not_4_out, not_5_out, not_6_out, not_7_out, not_8_out, not_9_out, not_10_out, not_11_out, not_12_out, not_13_out, not_14_out, not_15_out, not_16_out, not_17_out, not_18_out, not_19_out, not_20_out, not_21_out, not_22_out, not_23_out, not_24_out, not_25_out, not_26_out, not_27_out, not_28_out, not_29_out, not_30_out, not_31_out, not_32_out);
endmodule

module fullAdder (
  input  A,
  input  B,
  input  Cin,
  output Si,
  output Cout
);

  wire and_1_out, and_2_out, or_1_out, xor_1_out;

  xor xor_1 (xor_1_out, B, A);
  or or_1 (or_1_out, B, A);
  xor xor_2 (Si, Cin, xor_1_out);
  and and_1 (and_1_out, B, A);
  and and_2 (and_2_out, Cin, or_1_out);
  or or_2 (Cout, and_1_out, and_2_out);
endmodule

module somador (
  input  [31:0] A,
  input  [31:0] B,
  output [31:0] sSoma
);

  wire fulladder_1_cout, fulladder_2_cout, fulladder_3_cout, fulladder_4_cout, fulladder_5_cout,
       fulladder_6_cout, fulladder_7_cout, fulladder_8_cout, fulladder_9_cout, fulladder_10_cout,
       fulladder_11_cout, fulladder_12_cout, fulladder_13_cout, fulladder_14_cout, fulladder_15_cout,
       fulladder_16_cout, fulladder_17_cout, fulladder_18_cout, fulladder_19_cout, fulladder_20_cout,
       fulladder_21_cout, fulladder_22_cout, fulladder_23_cout, fulladder_24_cout, fulladder_25_cout,
       fulladder_26_cout, fulladder_27_cout, fulladder_28_cout, fulladder_29_cout, fulladder_30_cout,
       fulladder_31_cout, fulladder_32_cout;

  fullAdder fulladder_1 (.A(A[0]), .B(B[0]), .Cin(1'b0), .Si(sSoma[0]), .Cout(fulladder_1_cout));
  fullAdder fulladder_2 (.A(A[1]), .B(B[1]), .Cin(fulladder_1_cout), .Si(sSoma[1]), .Cout(fulladder_2_cout));
  fullAdder fulladder_3 (.A(A[2]), .B(B[2]), .Cin(fulladder_2_cout), .Si(sSoma[2]), .Cout(fulladder_3_cout));
  fullAdder fulladder_4 (.A(A[3]), .B(B[3]), .Cin(fulladder_3_cout), .Si(sSoma[3]), .Cout(fulladder_4_cout));
  fullAdder fulladder_5 (.A(A[4]), .B(B[4]), .Cin(fulladder_4_cout), .Si(sSoma[4]), .Cout(fulladder_5_cout));
  fullAdder fulladder_6 (.A(A[5]), .B(B[5]), .Cin(fulladder_5_cout), .Si(sSoma[5]), .Cout(fulladder_6_cout));
  fullAdder fulladder_7 (.A(A[6]), .B(B[6]), .Cin(fulladder_6_cout), .Si(sSoma[6]), .Cout(fulladder_7_cout));
  fullAdder fulladder_8 (.A(A[7]), .B(B[7]), .Cin(fulladder_7_cout), .Si(sSoma[7]), .Cout(fulladder_8_cout));
  fullAdder fulladder_9 (.A(A[8]), .B(B[8]), .Cin(fulladder_8_cout), .Si(sSoma[8]), .Cout(fulladder_9_cout));
  fullAdder fulladder_10 (.A(A[9]), .B(B[9]), .Cin(fulladder_9_cout), .Si(sSoma[9]), .Cout(fulladder_10_cout));
  fullAdder fulladder_11 (.A(A[10]), .B(B[10]), .Cin(fulladder_10_cout), .Si(sSoma[10]), .Cout(fulladder_11_cout));
  fullAdder fulladder_12 (.A(A[11]), .B(B[11]), .Cin(fulladder_11_cout), .Si(sSoma[11]), .Cout(fulladder_12_cout));
  fullAdder fulladder_13 (.A(A[12]), .B(B[12]), .Cin(fulladder_12_cout), .Si(sSoma[12]), .Cout(fulladder_13_cout));
  fullAdder fulladder_14 (.A(A[13]), .B(B[13]), .Cin(fulladder_13_cout), .Si(sSoma[13]), .Cout(fulladder_14_cout));
  fullAdder fulladder_15 (.A(A[14]), .B(B[14]), .Cin(fulladder_14_cout), .Si(sSoma[14]), .Cout(fulladder_15_cout));
  fullAdder fulladder_16 (.A(A[15]), .B(B[15]), .Cin(fulladder_15_cout), .Si(sSoma[15]), .Cout(fulladder_16_cout));
  fullAdder fulladder_17 (.A(A[16]), .B(B[16]), .Cin(fulladder_16_cout), .Si(sSoma[16]), .Cout(fulladder_17_cout));
  fullAdder fulladder_18 (.A(A[17]), .B(B[17]), .Cin(fulladder_17_cout), .Si(sSoma[17]), .Cout(fulladder_18_cout));
  fullAdder fulladder_19 (.A(A[18]), .B(B[18]), .Cin(fulladder_18_cout), .Si(sSoma[18]), .Cout(fulladder_19_cout));
  fullAdder fulladder_20 (.A(A[19]), .B(B[19]), .Cin(fulladder_19_cout), .Si(sSoma[19]), .Cout(fulladder_20_cout));
  fullAdder fulladder_21 (.A(A[20]), .B(B[20]), .Cin(fulladder_20_cout), .Si(sSoma[20]), .Cout(fulladder_21_cout));
  fullAdder fulladder_22 (.A(A[21]), .B(B[21]), .Cin(fulladder_21_cout), .Si(sSoma[21]), .Cout(fulladder_22_cout));
  fullAdder fulladder_23 (.A(A[22]), .B(B[22]), .Cin(fulladder_22_cout), .Si(sSoma[22]), .Cout(fulladder_23_cout));
  fullAdder fulladder_24 (.A(A[23]), .B(B[23]), .Cin(fulladder_23_cout), .Si(sSoma[23]), .Cout(fulladder_24_cout));
  fullAdder fulladder_25 (.A(A[24]), .B(B[24]), .Cin(fulladder_24_cout), .Si(sSoma[24]), .Cout(fulladder_25_cout));
  fullAdder fulladder_26 (.A(A[25]), .B(B[25]), .Cin(fulladder_25_cout), .Si(sSoma[25]), .Cout(fulladder_26_cout));
  fullAdder fulladder_27 (.A(A[26]), .B(B[26]), .Cin(fulladder_26_cout), .Si(sSoma[26]), .Cout(fulladder_27_cout));
  fullAdder fulladder_28 (.A(A[27]), .B(B[27]), .Cin(fulladder_27_cout), .Si(sSoma[27]), .Cout(fulladder_28_cout));
  fullAdder fulladder_29 (.A(A[28]), .B(B[28]), .Cin(fulladder_28_cout), .Si(sSoma[28]), .Cout(fulladder_29_cout));
  fullAdder fulladder_30 (.A(A[29]), .B(B[29]), .Cin(fulladder_29_cout), .Si(sSoma[29]), .Cout(fulladder_30_cout));
  fullAdder fulladder_31 (.A(A[30]), .B(B[30]), .Cin(fulladder_30_cout), .Si(sSoma[30]), .Cout(fulladder_31_cout));
  fullAdder fulladder_32 (.A(A[31]), .B(B[31]), .Cin(fulladder_31_cout), .Si(sSoma[31]), .Cout(fulladder_32_cout));
  // NoConnect on fulladder_32_cout

  // Other names for the same wires on the sheet: s0 = sSoma[0]; s1 = sSoma[1]; s2 = sSoma[2]; s3 = sSoma[3];
  //   s4 = sSoma[4]; s5 = sSoma[5]; s6 = sSoma[6]; s7 = sSoma[7]; s8 = sSoma[8]; s9 = sSoma[9]; s10 = sSoma[10];
  //   s11 = sSoma[11]; s12 = sSoma[12]; s13 = sSoma[13]; s14 = sSoma[14]; s15 = sSoma[15]; s16 = sSoma[16];
  //   s17 = sSoma[17]; s18 = sSoma[18]; s19 = sSoma[19]; s20 = sSoma[20]; s21 = sSoma[21]; s22 = sSoma[22];
  //   s23 = sSoma[23]; s24 = sSoma[24]; s25 = sSoma[25]; s26 = sSoma[26]; s27 = sSoma[27]; s28 = sSoma[28];
  //   s29 = sSoma[29]; s30 = sSoma[30]; s31 = sSoma[31]
endmodule

module subtrator (
  input  [31:0] A,
  input  [31:0] B,
  output [31:0] sSub
);

  wire fulladder_1_cout, fulladder_2_cout, fulladder_3_cout, fulladder_4_cout, fulladder_5_cout,
       fulladder_6_cout, fulladder_7_cout, fulladder_8_cout, fulladder_9_cout, fulladder_10_cout,
       fulladder_11_cout, fulladder_12_cout, fulladder_13_cout, fulladder_14_cout, fulladder_15_cout,
       fulladder_16_cout, fulladder_17_cout, fulladder_18_cout, fulladder_19_cout, fulladder_20_cout,
       fulladder_21_cout, fulladder_22_cout, fulladder_23_cout, fulladder_24_cout, fulladder_25_cout,
       fulladder_26_cout, fulladder_27_cout, fulladder_28_cout, fulladder_29_cout, fulladder_30_cout,
       fulladder_31_cout, fulladder_32_cout, not_1_out, not_2_out, not_3_out, not_4_out, not_5_out,
       not_6_out, not_7_out, not_8_out, not_9_out, not_10_out, not_11_out, not_12_out, not_13_out,
       not_14_out, not_15_out, not_16_out, not_17_out, not_18_out, not_19_out, not_20_out, not_21_out,
       not_22_out, not_23_out, not_24_out, not_25_out, not_26_out, not_27_out, not_28_out, not_29_out,
       not_30_out, not_31_out, not_32_out;

  not not_1 (not_1_out, B[0]);
  not not_2 (not_2_out, B[1]);
  not not_3 (not_3_out, B[2]);
  not not_4 (not_4_out, B[3]);
  not not_5 (not_5_out, B[4]);
  not not_6 (not_6_out, B[5]);
  not not_7 (not_7_out, B[6]);
  not not_8 (not_8_out, B[7]);
  not not_9 (not_9_out, B[8]);
  not not_10 (not_10_out, B[9]);
  not not_11 (not_11_out, B[10]);
  not not_12 (not_12_out, B[11]);
  not not_13 (not_13_out, B[12]);
  not not_14 (not_14_out, B[13]);
  not not_15 (not_15_out, B[14]);
  not not_16 (not_16_out, B[15]);
  fullAdder fulladder_1 (.A(A[0]), .B(not_1_out), .Cin(1'b1), .Si(sSub[0]), .Cout(fulladder_1_cout));
  fullAdder fulladder_2 (.A(A[1]), .B(not_2_out), .Cin(fulladder_1_cout), .Si(sSub[1]), .Cout(fulladder_2_cout));
  fullAdder fulladder_3 (.A(A[2]), .B(not_3_out), .Cin(fulladder_2_cout), .Si(sSub[2]), .Cout(fulladder_3_cout));
  fullAdder fulladder_4 (.A(A[3]), .B(not_4_out), .Cin(fulladder_3_cout), .Si(sSub[3]), .Cout(fulladder_4_cout));
  fullAdder fulladder_5 (.A(A[4]), .B(not_5_out), .Cin(fulladder_4_cout), .Si(sSub[4]), .Cout(fulladder_5_cout));
  fullAdder fulladder_6 (.A(A[5]), .B(not_6_out), .Cin(fulladder_5_cout), .Si(sSub[5]), .Cout(fulladder_6_cout));
  fullAdder fulladder_7 (.A(A[6]), .B(not_7_out), .Cin(fulladder_6_cout), .Si(sSub[6]), .Cout(fulladder_7_cout));
  fullAdder fulladder_8 (.A(A[7]), .B(not_8_out), .Cin(fulladder_7_cout), .Si(sSub[7]), .Cout(fulladder_8_cout));
  fullAdder fulladder_9 (.A(A[8]), .B(not_9_out), .Cin(fulladder_8_cout), .Si(sSub[8]), .Cout(fulladder_9_cout));
  fullAdder fulladder_10 (.A(A[9]), .B(not_10_out), .Cin(fulladder_9_cout), .Si(sSub[9]), .Cout(fulladder_10_cout));
  fullAdder fulladder_11 (.A(A[10]), .B(not_11_out), .Cin(fulladder_10_cout), .Si(sSub[10]), .Cout(fulladder_11_cout));
  fullAdder fulladder_12 (.A(A[11]), .B(not_12_out), .Cin(fulladder_11_cout), .Si(sSub[11]), .Cout(fulladder_12_cout));
  fullAdder fulladder_13 (.A(A[12]), .B(not_13_out), .Cin(fulladder_12_cout), .Si(sSub[12]), .Cout(fulladder_13_cout));
  fullAdder fulladder_14 (.A(A[13]), .B(not_14_out), .Cin(fulladder_13_cout), .Si(sSub[13]), .Cout(fulladder_14_cout));
  fullAdder fulladder_15 (.A(A[14]), .B(not_15_out), .Cin(fulladder_14_cout), .Si(sSub[14]), .Cout(fulladder_15_cout));
  fullAdder fulladder_16 (.A(A[15]), .B(not_16_out), .Cin(fulladder_15_cout), .Si(sSub[15]), .Cout(fulladder_16_cout));
  not not_17 (not_17_out, B[16]);
  not not_18 (not_18_out, B[17]);
  not not_19 (not_19_out, B[18]);
  not not_20 (not_20_out, B[19]);
  not not_21 (not_21_out, B[20]);
  not not_22 (not_22_out, B[21]);
  not not_23 (not_23_out, B[22]);
  not not_24 (not_24_out, B[23]);
  not not_25 (not_25_out, B[24]);
  not not_26 (not_26_out, B[25]);
  not not_27 (not_27_out, B[26]);
  not not_28 (not_28_out, B[27]);
  not not_29 (not_29_out, B[28]);
  not not_30 (not_30_out, B[29]);
  not not_31 (not_31_out, B[30]);
  not not_32 (not_32_out, B[31]);
  fullAdder fulladder_17 (.A(A[16]), .B(not_17_out), .Cin(fulladder_16_cout), .Si(sSub[16]), .Cout(fulladder_17_cout));
  fullAdder fulladder_18 (.A(A[17]), .B(not_18_out), .Cin(fulladder_17_cout), .Si(sSub[17]), .Cout(fulladder_18_cout));
  fullAdder fulladder_19 (.A(A[18]), .B(not_19_out), .Cin(fulladder_18_cout), .Si(sSub[18]), .Cout(fulladder_19_cout));
  fullAdder fulladder_20 (.A(A[19]), .B(not_20_out), .Cin(fulladder_19_cout), .Si(sSub[19]), .Cout(fulladder_20_cout));
  fullAdder fulladder_21 (.A(A[20]), .B(not_21_out), .Cin(fulladder_20_cout), .Si(sSub[20]), .Cout(fulladder_21_cout));
  fullAdder fulladder_22 (.A(A[21]), .B(not_22_out), .Cin(fulladder_21_cout), .Si(sSub[21]), .Cout(fulladder_22_cout));
  fullAdder fulladder_23 (.A(A[22]), .B(not_23_out), .Cin(fulladder_22_cout), .Si(sSub[22]), .Cout(fulladder_23_cout));
  fullAdder fulladder_24 (.A(A[23]), .B(not_24_out), .Cin(fulladder_23_cout), .Si(sSub[23]), .Cout(fulladder_24_cout));
  fullAdder fulladder_25 (.A(A[24]), .B(not_25_out), .Cin(fulladder_24_cout), .Si(sSub[24]), .Cout(fulladder_25_cout));
  fullAdder fulladder_26 (.A(A[25]), .B(not_26_out), .Cin(fulladder_25_cout), .Si(sSub[25]), .Cout(fulladder_26_cout));
  fullAdder fulladder_27 (.A(A[26]), .B(not_27_out), .Cin(fulladder_26_cout), .Si(sSub[26]), .Cout(fulladder_27_cout));
  fullAdder fulladder_28 (.A(A[27]), .B(not_28_out), .Cin(fulladder_27_cout), .Si(sSub[27]), .Cout(fulladder_28_cout));
  fullAdder fulladder_29 (.A(A[28]), .B(not_29_out), .Cin(fulladder_28_cout), .Si(sSub[28]), .Cout(fulladder_29_cout));
  fullAdder fulladder_30 (.A(A[29]), .B(not_30_out), .Cin(fulladder_29_cout), .Si(sSub[29]), .Cout(fulladder_30_cout));
  fullAdder fulladder_31 (.A(A[30]), .B(not_31_out), .Cin(fulladder_30_cout), .Si(sSub[30]), .Cout(fulladder_31_cout));
  fullAdder fulladder_32 (.A(A[31]), .B(not_32_out), .Cin(fulladder_31_cout), .Si(sSub[31]), .Cout(fulladder_32_cout));
  // NoConnect on fulladder_32_cout

  // Other names for the same wires on the sheet: s0 = sSub[0]; s1 = sSub[1]; s2 = sSub[2]; s3 = sSub[3]; s4 = sSub[4];
  //   s5 = sSub[5]; s6 = sSub[6]; s7 = sSub[7]; s8 = sSub[8]; s9 = sSub[9]; s10 = sSub[10]; s11 = sSub[11];
  //   s12 = sSub[12]; s13 = sSub[13]; s14 = sSub[14]; s15 = sSub[15]; s16 = sSub[16]; s17 = sSub[17]; s18 = sSub[18];
  //   s19 = sSub[19]; s20 = sSub[20]; s21 = sSub[21]; s22 = sSub[22]; s23 = sSub[23]; s24 = sSub[24]; s25 = sSub[25];
  //   s26 = sSub[26]; s27 = sSub[27]; s28 = sSub[28]; s29 = sSub[29]; s30 = sSub[30]; s31 = sSub[31]
endmodule

module multiplicador (
  input  [31:0] A,
  input  [31:0] B,
  output [31:0] sMult
);

  Multiplier #(.width(32)) multiplier_1 (.a(A), .b(B), .out(sMult));  // open: cin, cout
endmodule

module ulaAND (
  input  [31:0] A,
  input  [31:0] B,
  output [31:0] sAND
);

  assign sAND = A & B;  // AND_Gate and_1, 32 bits wide
endmodule

module ulaOR (
  input  [31:0] A,
  input  [31:0] B,
  output [31:0] sOR
);

  assign sOR = A | B;  // OR_Gate or_1, 32 bits wide
endmodule

module ulaXOR (
  input  [31:0] A,
  input  [31:0] B,
  output [31:0] sXOR
);

  assign sXOR = A ^ B;  // XOR_Gate xor_1, 32 bits wide
endmodule

module deslocEsq (
  input  [31:0] A,
  input  [31:0] B,
  output [31:0] sDesl
);

  wire multiplexer_1_out, multiplexer_2_out, multiplexer_3_out, multiplexer_4_out, multiplexer_5_out,
       multiplexer_6_out, multiplexer_7_out, multiplexer_8_out, multiplexer_9_out, multiplexer_10_out,
       multiplexer_11_out, multiplexer_12_out, multiplexer_13_out, multiplexer_14_out, multiplexer_15_out,
       multiplexer_16_out, multiplexer_17_out, multiplexer_18_out, multiplexer_19_out, multiplexer_20_out,
       multiplexer_21_out, multiplexer_22_out, multiplexer_23_out, multiplexer_24_out, multiplexer_25_out,
       multiplexer_26_out, multiplexer_27_out, multiplexer_28_out, multiplexer_29_out, multiplexer_30_out,
       multiplexer_31_out, multiplexer_32_out, multiplexer_33_out, multiplexer_34_out, multiplexer_35_out,
       multiplexer_36_out, multiplexer_37_out, multiplexer_38_out, multiplexer_39_out, multiplexer_40_out,
       multiplexer_41_out, multiplexer_42_out, multiplexer_43_out, multiplexer_44_out, multiplexer_45_out,
       multiplexer_46_out, multiplexer_47_out, multiplexer_48_out, multiplexer_49_out, multiplexer_50_out,
       multiplexer_51_out, multiplexer_52_out, multiplexer_53_out, multiplexer_54_out, multiplexer_55_out,
       multiplexer_56_out, multiplexer_57_out, multiplexer_58_out, multiplexer_59_out, multiplexer_60_out,
       multiplexer_61_out, multiplexer_62_out, multiplexer_63_out, multiplexer_64_out, multiplexer_65_out,
       multiplexer_66_out, multiplexer_67_out, multiplexer_68_out, multiplexer_69_out, multiplexer_70_out,
       multiplexer_71_out, multiplexer_72_out, multiplexer_73_out, multiplexer_74_out, multiplexer_75_out,
       multiplexer_76_out, multiplexer_77_out, multiplexer_78_out, multiplexer_79_out, multiplexer_80_out,
       multiplexer_81_out, multiplexer_82_out, multiplexer_83_out, multiplexer_84_out, multiplexer_85_out,
       multiplexer_86_out, multiplexer_87_out, multiplexer_88_out, multiplexer_89_out, multiplexer_90_out,
       multiplexer_91_out, multiplexer_92_out, multiplexer_93_out, multiplexer_94_out, multiplexer_95_out,
       multiplexer_96_out, multiplexer_97_out, multiplexer_98_out, multiplexer_99_out, multiplexer_100_out,
       multiplexer_101_out, multiplexer_102_out, multiplexer_103_out, multiplexer_104_out,
       multiplexer_105_out, multiplexer_106_out, multiplexer_107_out, multiplexer_108_out,
       multiplexer_109_out, multiplexer_110_out, multiplexer_111_out, multiplexer_112_out,
       multiplexer_113_out, multiplexer_114_out, multiplexer_115_out, multiplexer_116_out,
       multiplexer_117_out, multiplexer_118_out, multiplexer_119_out, multiplexer_120_out,
       multiplexer_121_out, multiplexer_122_out, multiplexer_123_out, multiplexer_124_out,
       multiplexer_125_out, multiplexer_126_out, multiplexer_127_out, multiplexer_128_out,
       multiplexer_129_out, multiplexer_130_out, multiplexer_131_out, multiplexer_132_out,
       multiplexer_133_out, multiplexer_134_out, multiplexer_135_out, multiplexer_136_out,
       multiplexer_137_out, multiplexer_138_out, multiplexer_139_out, multiplexer_140_out,
       multiplexer_141_out, multiplexer_142_out, multiplexer_143_out, multiplexer_144_out,
       multiplexer_145_out, multiplexer_146_out, multiplexer_147_out, multiplexer_148_out,
       multiplexer_149_out, multiplexer_150_out, multiplexer_151_out, multiplexer_152_out,
       multiplexer_153_out, multiplexer_154_out, multiplexer_155_out, multiplexer_156_out,
       multiplexer_157_out, multiplexer_158_out, multiplexer_159_out, multiplexer_160_out, or_1_out;

  Multiplexer multiplexer_1 (.in0(A[0]), .in1(1'b0), .out(multiplexer_1_out), .sel(B[0]));
  Multiplexer multiplexer_2 (.in0(A[1]), .in1(A[0]), .out(multiplexer_2_out), .sel(B[0]));
  Multiplexer multiplexer_3 (.in0(A[2]), .in1(A[1]), .out(multiplexer_3_out), .sel(B[0]));
  Multiplexer multiplexer_4 (.in0(A[3]), .in1(A[2]), .out(multiplexer_4_out), .sel(B[0]));
  Multiplexer multiplexer_5 (.in0(A[4]), .in1(A[3]), .out(multiplexer_5_out), .sel(B[0]));
  Multiplexer multiplexer_6 (.in0(A[5]), .in1(A[4]), .out(multiplexer_6_out), .sel(B[0]));
  Multiplexer multiplexer_7 (.in0(A[6]), .in1(A[5]), .out(multiplexer_7_out), .sel(B[0]));
  Multiplexer multiplexer_8 (.in0(A[7]), .in1(A[6]), .out(multiplexer_8_out), .sel(B[0]));
  Multiplexer multiplexer_9 (.in0(A[8]), .in1(A[7]), .out(multiplexer_9_out), .sel(B[0]));
  Multiplexer multiplexer_10 (.in0(A[9]), .in1(A[8]), .out(multiplexer_10_out), .sel(B[0]));
  Multiplexer multiplexer_11 (.in0(A[10]), .in1(A[9]), .out(multiplexer_11_out), .sel(B[0]));
  Multiplexer multiplexer_12 (.in0(A[11]), .in1(A[10]), .out(multiplexer_12_out), .sel(B[0]));
  Multiplexer multiplexer_13 (.in0(A[12]), .in1(A[11]), .out(multiplexer_13_out), .sel(B[0]));
  Multiplexer multiplexer_14 (.in0(A[13]), .in1(A[12]), .out(multiplexer_14_out), .sel(B[0]));
  Multiplexer multiplexer_15 (.in0(A[14]), .in1(A[13]), .out(multiplexer_15_out), .sel(B[0]));
  Multiplexer multiplexer_16 (.in0(A[15]), .in1(A[14]), .out(multiplexer_16_out), .sel(B[0]));
  Multiplexer multiplexer_17 (.in0(A[16]), .in1(A[15]), .out(multiplexer_17_out), .sel(B[0]));
  Multiplexer multiplexer_18 (.in0(A[17]), .in1(A[16]), .out(multiplexer_18_out), .sel(B[0]));
  Multiplexer multiplexer_19 (.in0(A[18]), .in1(A[17]), .out(multiplexer_19_out), .sel(B[0]));
  Multiplexer multiplexer_20 (.in0(A[19]), .in1(A[18]), .out(multiplexer_20_out), .sel(B[0]));
  Multiplexer multiplexer_21 (.in0(A[20]), .in1(A[19]), .out(multiplexer_21_out), .sel(B[0]));
  Multiplexer multiplexer_22 (.in0(A[21]), .in1(A[20]), .out(multiplexer_22_out), .sel(B[0]));
  Multiplexer multiplexer_23 (.in0(A[22]), .in1(A[21]), .out(multiplexer_23_out), .sel(B[0]));
  Multiplexer multiplexer_24 (.in0(A[23]), .in1(A[22]), .out(multiplexer_24_out), .sel(B[0]));
  Multiplexer multiplexer_25 (.in0(A[24]), .in1(A[23]), .out(multiplexer_25_out), .sel(B[0]));
  Multiplexer multiplexer_26 (.in0(A[25]), .in1(A[24]), .out(multiplexer_26_out), .sel(B[0]));
  Multiplexer multiplexer_27 (.in0(A[26]), .in1(A[25]), .out(multiplexer_27_out), .sel(B[0]));
  Multiplexer multiplexer_28 (.in0(A[27]), .in1(A[26]), .out(multiplexer_28_out), .sel(B[0]));
  Multiplexer multiplexer_29 (.in0(A[28]), .in1(A[27]), .out(multiplexer_29_out), .sel(B[0]));
  Multiplexer multiplexer_30 (.in0(A[29]), .in1(A[28]), .out(multiplexer_30_out), .sel(B[0]));
  Multiplexer multiplexer_31 (.in0(A[30]), .in1(A[29]), .out(multiplexer_31_out), .sel(B[0]));
  Multiplexer multiplexer_32 (.in0(A[31]), .in1(A[30]), .out(multiplexer_32_out), .sel(B[0]));
  Multiplexer multiplexer_33 (.in0(multiplexer_1_out), .in1(1'b0), .out(multiplexer_33_out), .sel(B[1]));
  Multiplexer multiplexer_34 (.in0(multiplexer_2_out), .in1(1'b0), .out(multiplexer_34_out), .sel(B[1]));
  Multiplexer multiplexer_35 (.in0(multiplexer_3_out), .in1(multiplexer_1_out), .out(multiplexer_35_out), .sel(B[1]));
  Multiplexer multiplexer_36 (.in0(multiplexer_4_out), .in1(multiplexer_2_out), .out(multiplexer_36_out), .sel(B[1]));
  Multiplexer multiplexer_37 (.in0(multiplexer_5_out), .in1(multiplexer_3_out), .out(multiplexer_37_out), .sel(B[1]));
  Multiplexer multiplexer_38 (.in0(multiplexer_6_out), .in1(multiplexer_4_out), .out(multiplexer_38_out), .sel(B[1]));
  Multiplexer multiplexer_39 (.in0(multiplexer_7_out), .in1(multiplexer_5_out), .out(multiplexer_39_out), .sel(B[1]));
  Multiplexer multiplexer_40 (.in0(multiplexer_8_out), .in1(multiplexer_6_out), .out(multiplexer_40_out), .sel(B[1]));
  Multiplexer multiplexer_41 (.in0(multiplexer_9_out), .in1(multiplexer_7_out), .out(multiplexer_41_out), .sel(B[1]));
  Multiplexer multiplexer_42 (.in0(multiplexer_10_out), .in1(multiplexer_8_out), .out(multiplexer_42_out), .sel(B[1]));
  Multiplexer multiplexer_43 (.in0(multiplexer_11_out), .in1(multiplexer_9_out), .out(multiplexer_43_out), .sel(B[1]));
  Multiplexer multiplexer_44 (.in0(multiplexer_12_out), .in1(multiplexer_10_out), .out(multiplexer_44_out), .sel(B[1]));
  Multiplexer multiplexer_45 (.in0(multiplexer_13_out), .in1(multiplexer_11_out), .out(multiplexer_45_out), .sel(B[1]));
  Multiplexer multiplexer_46 (.in0(multiplexer_14_out), .in1(multiplexer_12_out), .out(multiplexer_46_out), .sel(B[1]));
  Multiplexer multiplexer_47 (.in0(multiplexer_15_out), .in1(multiplexer_13_out), .out(multiplexer_47_out), .sel(B[1]));
  Multiplexer multiplexer_48 (.in0(multiplexer_16_out), .in1(multiplexer_14_out), .out(multiplexer_48_out), .sel(B[1]));
  Multiplexer multiplexer_49 (.in0(multiplexer_17_out), .in1(multiplexer_15_out), .out(multiplexer_49_out), .sel(B[1]));
  Multiplexer multiplexer_50 (.in0(multiplexer_18_out), .in1(multiplexer_16_out), .out(multiplexer_50_out), .sel(B[1]));
  Multiplexer multiplexer_51 (.in0(multiplexer_19_out), .in1(multiplexer_17_out), .out(multiplexer_51_out), .sel(B[1]));
  Multiplexer multiplexer_52 (.in0(multiplexer_20_out), .in1(multiplexer_18_out), .out(multiplexer_52_out), .sel(B[1]));
  Multiplexer multiplexer_53 (.in0(multiplexer_21_out), .in1(multiplexer_19_out), .out(multiplexer_53_out), .sel(B[1]));
  Multiplexer multiplexer_54 (.in0(multiplexer_22_out), .in1(multiplexer_20_out), .out(multiplexer_54_out), .sel(B[1]));
  Multiplexer multiplexer_55 (.in0(multiplexer_23_out), .in1(multiplexer_21_out), .out(multiplexer_55_out), .sel(B[1]));
  Multiplexer multiplexer_56 (.in0(multiplexer_24_out), .in1(multiplexer_22_out), .out(multiplexer_56_out), .sel(B[1]));
  Multiplexer multiplexer_57 (.in0(multiplexer_25_out), .in1(multiplexer_23_out), .out(multiplexer_57_out), .sel(B[1]));
  Multiplexer multiplexer_58 (.in0(multiplexer_26_out), .in1(multiplexer_24_out), .out(multiplexer_58_out), .sel(B[1]));
  Multiplexer multiplexer_59 (.in0(multiplexer_27_out), .in1(multiplexer_25_out), .out(multiplexer_59_out), .sel(B[1]));
  Multiplexer multiplexer_60 (.in0(multiplexer_28_out), .in1(multiplexer_26_out), .out(multiplexer_60_out), .sel(B[1]));
  Multiplexer multiplexer_61 (.in0(multiplexer_29_out), .in1(multiplexer_27_out), .out(multiplexer_61_out), .sel(B[1]));
  Multiplexer multiplexer_62 (.in0(multiplexer_30_out), .in1(multiplexer_28_out), .out(multiplexer_62_out), .sel(B[1]));
  Multiplexer multiplexer_63 (.in0(multiplexer_31_out), .in1(multiplexer_29_out), .out(multiplexer_63_out), .sel(B[1]));
  Multiplexer multiplexer_64 (.in0(multiplexer_32_out), .in1(multiplexer_30_out), .out(multiplexer_64_out), .sel(B[1]));
  Multiplexer multiplexer_65 (.in0(multiplexer_33_out), .in1(1'b0), .out(multiplexer_65_out), .sel(B[2]));
  Multiplexer multiplexer_66 (.in0(multiplexer_34_out), .in1(1'b0), .out(multiplexer_66_out), .sel(B[2]));
  Multiplexer multiplexer_67 (.in0(multiplexer_35_out), .in1(1'b0), .out(multiplexer_67_out), .sel(B[2]));
  Multiplexer multiplexer_68 (.in0(multiplexer_36_out), .in1(1'b0), .out(multiplexer_68_out), .sel(B[2]));
  Multiplexer multiplexer_69 (.in0(multiplexer_37_out), .in1(multiplexer_33_out), .out(multiplexer_69_out), .sel(B[2]));
  Multiplexer multiplexer_70 (.in0(multiplexer_38_out), .in1(multiplexer_34_out), .out(multiplexer_70_out), .sel(B[2]));
  Multiplexer multiplexer_71 (.in0(multiplexer_39_out), .in1(multiplexer_35_out), .out(multiplexer_71_out), .sel(B[2]));
  Multiplexer multiplexer_72 (.in0(multiplexer_40_out), .in1(multiplexer_36_out), .out(multiplexer_72_out), .sel(B[2]));
  Multiplexer multiplexer_73 (.in0(multiplexer_41_out), .in1(multiplexer_37_out), .out(multiplexer_73_out), .sel(B[2]));
  Multiplexer multiplexer_74 (.in0(multiplexer_42_out), .in1(multiplexer_38_out), .out(multiplexer_74_out), .sel(B[2]));
  Multiplexer multiplexer_75 (.in0(multiplexer_43_out), .in1(multiplexer_39_out), .out(multiplexer_75_out), .sel(B[2]));
  Multiplexer multiplexer_76 (.in0(multiplexer_44_out), .in1(multiplexer_40_out), .out(multiplexer_76_out), .sel(B[2]));
  Multiplexer multiplexer_77 (.in0(multiplexer_45_out), .in1(multiplexer_41_out), .out(multiplexer_77_out), .sel(B[2]));
  Multiplexer multiplexer_78 (.in0(multiplexer_46_out), .in1(multiplexer_42_out), .out(multiplexer_78_out), .sel(B[2]));
  Multiplexer multiplexer_79 (.in0(multiplexer_47_out), .in1(multiplexer_43_out), .out(multiplexer_79_out), .sel(B[2]));
  Multiplexer multiplexer_80 (.in0(multiplexer_48_out), .in1(multiplexer_44_out), .out(multiplexer_80_out), .sel(B[2]));
  Multiplexer multiplexer_81 (.in0(multiplexer_49_out), .in1(multiplexer_45_out), .out(multiplexer_81_out), .sel(B[2]));
  Multiplexer multiplexer_82 (.in0(multiplexer_50_out), .in1(multiplexer_46_out), .out(multiplexer_82_out), .sel(B[2]));
  Multiplexer multiplexer_83 (.in0(multiplexer_51_out), .in1(multiplexer_47_out), .out(multiplexer_83_out), .sel(B[2]));
  Multiplexer multiplexer_84 (.in0(multiplexer_52_out), .in1(multiplexer_48_out), .out(multiplexer_84_out), .sel(B[2]));
  Multiplexer multiplexer_85 (.in0(multiplexer_53_out), .in1(multiplexer_49_out), .out(multiplexer_85_out), .sel(B[2]));
  Multiplexer multiplexer_86 (.in0(multiplexer_54_out), .in1(multiplexer_50_out), .out(multiplexer_86_out), .sel(B[2]));
  Multiplexer multiplexer_87 (.in0(multiplexer_55_out), .in1(multiplexer_51_out), .out(multiplexer_87_out), .sel(B[2]));
  Multiplexer multiplexer_88 (.in0(multiplexer_56_out), .in1(multiplexer_52_out), .out(multiplexer_88_out), .sel(B[2]));
  Multiplexer multiplexer_89 (.in0(multiplexer_57_out), .in1(multiplexer_53_out), .out(multiplexer_89_out), .sel(B[2]));
  Multiplexer multiplexer_90 (.in0(multiplexer_58_out), .in1(multiplexer_54_out), .out(multiplexer_90_out), .sel(B[2]));
  Multiplexer multiplexer_91 (.in0(multiplexer_59_out), .in1(multiplexer_55_out), .out(multiplexer_91_out), .sel(B[2]));
  Multiplexer multiplexer_92 (.in0(multiplexer_60_out), .in1(multiplexer_56_out), .out(multiplexer_92_out), .sel(B[2]));
  Multiplexer multiplexer_93 (.in0(multiplexer_61_out), .in1(multiplexer_57_out), .out(multiplexer_93_out), .sel(B[2]));
  Multiplexer multiplexer_94 (.in0(multiplexer_62_out), .in1(multiplexer_58_out), .out(multiplexer_94_out), .sel(B[2]));
  Multiplexer multiplexer_95 (.in0(multiplexer_63_out), .in1(multiplexer_59_out), .out(multiplexer_95_out), .sel(B[2]));
  Multiplexer multiplexer_96 (.in0(multiplexer_64_out), .in1(multiplexer_60_out), .out(multiplexer_96_out), .sel(B[2]));
  Multiplexer multiplexer_97 (.in0(multiplexer_65_out), .in1(1'b0), .out(multiplexer_97_out), .sel(B[3]));
  Multiplexer multiplexer_98 (.in0(multiplexer_66_out), .in1(1'b0), .out(multiplexer_98_out), .sel(B[3]));
  Multiplexer multiplexer_99 (.in0(multiplexer_67_out), .in1(1'b0), .out(multiplexer_99_out), .sel(B[3]));
  Multiplexer multiplexer_100 (.in0(multiplexer_68_out), .in1(1'b0), .out(multiplexer_100_out), .sel(B[3]));
  Multiplexer multiplexer_101 (.in0(multiplexer_69_out), .in1(1'b0), .out(multiplexer_101_out), .sel(B[3]));
  Multiplexer multiplexer_102 (.in0(multiplexer_70_out), .in1(1'b0), .out(multiplexer_102_out), .sel(B[3]));
  Multiplexer multiplexer_103 (.in0(multiplexer_71_out), .in1(1'b0), .out(multiplexer_103_out), .sel(B[3]));
  Multiplexer multiplexer_104 (.in0(multiplexer_72_out), .in1(1'b0), .out(multiplexer_104_out), .sel(B[3]));
  Multiplexer multiplexer_105 (
    .in0(multiplexer_73_out), .in1(multiplexer_65_out), .out(multiplexer_105_out), .sel(B[3]));
  Multiplexer multiplexer_106 (
    .in0(multiplexer_74_out), .in1(multiplexer_66_out), .out(multiplexer_106_out), .sel(B[3]));
  Multiplexer multiplexer_107 (
    .in0(multiplexer_75_out), .in1(multiplexer_67_out), .out(multiplexer_107_out), .sel(B[3]));
  Multiplexer multiplexer_108 (
    .in0(multiplexer_76_out), .in1(multiplexer_68_out), .out(multiplexer_108_out), .sel(B[3]));
  Multiplexer multiplexer_109 (
    .in0(multiplexer_77_out), .in1(multiplexer_69_out), .out(multiplexer_109_out), .sel(B[3]));
  Multiplexer multiplexer_110 (
    .in0(multiplexer_78_out), .in1(multiplexer_70_out), .out(multiplexer_110_out), .sel(B[3]));
  Multiplexer multiplexer_111 (
    .in0(multiplexer_79_out), .in1(multiplexer_71_out), .out(multiplexer_111_out), .sel(B[3]));
  Multiplexer multiplexer_112 (
    .in0(multiplexer_80_out), .in1(multiplexer_72_out), .out(multiplexer_112_out), .sel(B[3]));
  Multiplexer multiplexer_113 (
    .in0(multiplexer_81_out), .in1(multiplexer_73_out), .out(multiplexer_113_out), .sel(B[3]));
  Multiplexer multiplexer_114 (
    .in0(multiplexer_82_out), .in1(multiplexer_74_out), .out(multiplexer_114_out), .sel(B[3]));
  Multiplexer multiplexer_115 (
    .in0(multiplexer_83_out), .in1(multiplexer_75_out), .out(multiplexer_115_out), .sel(B[3]));
  Multiplexer multiplexer_116 (
    .in0(multiplexer_84_out), .in1(multiplexer_76_out), .out(multiplexer_116_out), .sel(B[3]));
  Multiplexer multiplexer_117 (
    .in0(multiplexer_85_out), .in1(multiplexer_77_out), .out(multiplexer_117_out), .sel(B[3]));
  Multiplexer multiplexer_118 (
    .in0(multiplexer_86_out), .in1(multiplexer_78_out), .out(multiplexer_118_out), .sel(B[3]));
  Multiplexer multiplexer_119 (
    .in0(multiplexer_87_out), .in1(multiplexer_79_out), .out(multiplexer_119_out), .sel(B[3]));
  Multiplexer multiplexer_120 (
    .in0(multiplexer_88_out), .in1(multiplexer_80_out), .out(multiplexer_120_out), .sel(B[3]));
  Multiplexer multiplexer_121 (
    .in0(multiplexer_89_out), .in1(multiplexer_81_out), .out(multiplexer_121_out), .sel(B[3]));
  Multiplexer multiplexer_122 (
    .in0(multiplexer_90_out), .in1(multiplexer_82_out), .out(multiplexer_122_out), .sel(B[3]));
  Multiplexer multiplexer_123 (
    .in0(multiplexer_91_out), .in1(multiplexer_83_out), .out(multiplexer_123_out), .sel(B[3]));
  Multiplexer multiplexer_124 (
    .in0(multiplexer_92_out), .in1(multiplexer_84_out), .out(multiplexer_124_out), .sel(B[3]));
  Multiplexer multiplexer_125 (
    .in0(multiplexer_93_out), .in1(multiplexer_85_out), .out(multiplexer_125_out), .sel(B[3]));
  Multiplexer multiplexer_126 (
    .in0(multiplexer_94_out), .in1(multiplexer_86_out), .out(multiplexer_126_out), .sel(B[3]));
  Multiplexer multiplexer_127 (
    .in0(multiplexer_95_out), .in1(multiplexer_87_out), .out(multiplexer_127_out), .sel(B[3]));
  Multiplexer multiplexer_128 (
    .in0(multiplexer_96_out), .in1(multiplexer_88_out), .out(multiplexer_128_out), .sel(B[3]));
  Multiplexer multiplexer_129 (.in0(multiplexer_97_out), .in1(1'b0), .out(multiplexer_129_out), .sel(B[4]));
  Multiplexer multiplexer_130 (.in0(multiplexer_98_out), .in1(1'b0), .out(multiplexer_130_out), .sel(B[4]));
  Multiplexer multiplexer_131 (.in0(multiplexer_99_out), .in1(1'b0), .out(multiplexer_131_out), .sel(B[4]));
  Multiplexer multiplexer_132 (.in0(multiplexer_100_out), .in1(1'b0), .out(multiplexer_132_out), .sel(B[4]));
  Multiplexer multiplexer_133 (.in0(multiplexer_101_out), .in1(1'b0), .out(multiplexer_133_out), .sel(B[4]));
  Multiplexer multiplexer_134 (.in0(multiplexer_102_out), .in1(1'b0), .out(multiplexer_134_out), .sel(B[4]));
  Multiplexer multiplexer_135 (.in0(multiplexer_103_out), .in1(1'b0), .out(multiplexer_135_out), .sel(B[4]));
  Multiplexer multiplexer_136 (.in0(multiplexer_104_out), .in1(1'b0), .out(multiplexer_136_out), .sel(B[4]));
  Multiplexer multiplexer_137 (.in0(multiplexer_105_out), .in1(1'b0), .out(multiplexer_137_out), .sel(B[4]));
  Multiplexer multiplexer_138 (.in0(multiplexer_106_out), .in1(1'b0), .out(multiplexer_138_out), .sel(B[4]));
  Multiplexer multiplexer_139 (.in0(multiplexer_107_out), .in1(1'b0), .out(multiplexer_139_out), .sel(B[4]));
  Multiplexer multiplexer_140 (.in0(multiplexer_108_out), .in1(1'b0), .out(multiplexer_140_out), .sel(B[4]));
  Multiplexer multiplexer_141 (.in0(multiplexer_109_out), .in1(1'b0), .out(multiplexer_141_out), .sel(B[4]));
  Multiplexer multiplexer_142 (.in0(multiplexer_110_out), .in1(1'b0), .out(multiplexer_142_out), .sel(B[4]));
  Multiplexer multiplexer_143 (.in0(multiplexer_111_out), .in1(1'b0), .out(multiplexer_143_out), .sel(B[4]));
  Multiplexer multiplexer_144 (.in0(multiplexer_112_out), .in1(1'b0), .out(multiplexer_144_out), .sel(B[4]));
  Multiplexer multiplexer_145 (
    .in0(multiplexer_113_out), .in1(multiplexer_97_out), .out(multiplexer_145_out), .sel(B[4]));
  Multiplexer multiplexer_146 (
    .in0(multiplexer_114_out), .in1(multiplexer_98_out), .out(multiplexer_146_out), .sel(B[4]));
  Multiplexer multiplexer_147 (
    .in0(multiplexer_115_out), .in1(multiplexer_99_out), .out(multiplexer_147_out), .sel(B[4]));
  Multiplexer multiplexer_148 (
    .in0(multiplexer_116_out), .in1(multiplexer_100_out), .out(multiplexer_148_out), .sel(B[4]));
  Multiplexer multiplexer_149 (
    .in0(multiplexer_117_out), .in1(multiplexer_101_out), .out(multiplexer_149_out), .sel(B[4]));
  Multiplexer multiplexer_150 (
    .in0(multiplexer_118_out), .in1(multiplexer_102_out), .out(multiplexer_150_out), .sel(B[4]));
  Multiplexer multiplexer_151 (
    .in0(multiplexer_119_out), .in1(multiplexer_103_out), .out(multiplexer_151_out), .sel(B[4]));
  Multiplexer multiplexer_152 (
    .in0(multiplexer_120_out), .in1(multiplexer_104_out), .out(multiplexer_152_out), .sel(B[4]));
  Multiplexer multiplexer_153 (
    .in0(multiplexer_121_out), .in1(multiplexer_105_out), .out(multiplexer_153_out), .sel(B[4]));
  Multiplexer multiplexer_154 (
    .in0(multiplexer_122_out), .in1(multiplexer_106_out), .out(multiplexer_154_out), .sel(B[4]));
  Multiplexer multiplexer_155 (
    .in0(multiplexer_123_out), .in1(multiplexer_107_out), .out(multiplexer_155_out), .sel(B[4]));
  Multiplexer multiplexer_156 (
    .in0(multiplexer_124_out), .in1(multiplexer_108_out), .out(multiplexer_156_out), .sel(B[4]));
  Multiplexer multiplexer_157 (
    .in0(multiplexer_125_out), .in1(multiplexer_109_out), .out(multiplexer_157_out), .sel(B[4]));
  Multiplexer multiplexer_158 (
    .in0(multiplexer_126_out), .in1(multiplexer_110_out), .out(multiplexer_158_out), .sel(B[4]));
  Multiplexer multiplexer_159 (
    .in0(multiplexer_127_out), .in1(multiplexer_111_out), .out(multiplexer_159_out), .sel(B[4]));
  Multiplexer multiplexer_160 (
    .in0(multiplexer_128_out), .in1(multiplexer_112_out), .out(multiplexer_160_out), .sel(B[4]));
  Multiplexer multiplexer_161 (.in0(multiplexer_129_out), .in1(1'b0), .out(sDesl[0]), .sel(or_1_out));
  Multiplexer multiplexer_162 (.in0(multiplexer_130_out), .in1(1'b0), .out(sDesl[1]), .sel(or_1_out));
  Multiplexer multiplexer_163 (.in0(multiplexer_131_out), .in1(1'b0), .out(sDesl[2]), .sel(or_1_out));
  Multiplexer multiplexer_164 (.in0(multiplexer_132_out), .in1(1'b0), .out(sDesl[3]), .sel(or_1_out));
  Multiplexer multiplexer_165 (.in0(multiplexer_133_out), .in1(1'b0), .out(sDesl[4]), .sel(or_1_out));
  Multiplexer multiplexer_166 (.in0(multiplexer_134_out), .in1(1'b0), .out(sDesl[5]), .sel(or_1_out));
  Multiplexer multiplexer_167 (.in0(multiplexer_135_out), .in1(1'b0), .out(sDesl[6]), .sel(or_1_out));
  Multiplexer multiplexer_168 (.in0(multiplexer_136_out), .in1(1'b0), .out(sDesl[7]), .sel(or_1_out));
  Multiplexer multiplexer_169 (.in0(multiplexer_137_out), .in1(1'b0), .out(sDesl[8]), .sel(or_1_out));
  Multiplexer multiplexer_170 (.in0(multiplexer_138_out), .in1(1'b0), .out(sDesl[9]), .sel(or_1_out));
  Multiplexer multiplexer_171 (.in0(multiplexer_139_out), .in1(1'b0), .out(sDesl[10]), .sel(or_1_out));
  Multiplexer multiplexer_172 (.in0(multiplexer_140_out), .in1(1'b0), .out(sDesl[11]), .sel(or_1_out));
  Multiplexer multiplexer_173 (.in0(multiplexer_141_out), .in1(1'b0), .out(sDesl[12]), .sel(or_1_out));
  Multiplexer multiplexer_174 (.in0(multiplexer_142_out), .in1(1'b0), .out(sDesl[13]), .sel(or_1_out));
  Multiplexer multiplexer_175 (.in0(multiplexer_143_out), .in1(1'b0), .out(sDesl[14]), .sel(or_1_out));
  Multiplexer multiplexer_176 (.in0(multiplexer_144_out), .in1(1'b0), .out(sDesl[15]), .sel(or_1_out));
  Multiplexer multiplexer_177 (.in0(multiplexer_145_out), .in1(1'b0), .out(sDesl[16]), .sel(or_1_out));
  Multiplexer multiplexer_178 (.in0(multiplexer_146_out), .in1(1'b0), .out(sDesl[17]), .sel(or_1_out));
  Multiplexer multiplexer_179 (.in0(multiplexer_147_out), .in1(1'b0), .out(sDesl[18]), .sel(or_1_out));
  Multiplexer multiplexer_180 (.in0(multiplexer_148_out), .in1(1'b0), .out(sDesl[19]), .sel(or_1_out));
  Multiplexer multiplexer_181 (.in0(multiplexer_149_out), .in1(1'b0), .out(sDesl[20]), .sel(or_1_out));
  Multiplexer multiplexer_182 (.in0(multiplexer_150_out), .in1(1'b0), .out(sDesl[21]), .sel(or_1_out));
  Multiplexer multiplexer_183 (.in0(multiplexer_151_out), .in1(1'b0), .out(sDesl[22]), .sel(or_1_out));
  Multiplexer multiplexer_184 (.in0(multiplexer_152_out), .in1(1'b0), .out(sDesl[23]), .sel(or_1_out));
  Multiplexer multiplexer_185 (.in0(multiplexer_153_out), .in1(1'b0), .out(sDesl[24]), .sel(or_1_out));
  Multiplexer multiplexer_186 (.in0(multiplexer_154_out), .in1(1'b0), .out(sDesl[25]), .sel(or_1_out));
  Multiplexer multiplexer_187 (.in0(multiplexer_155_out), .in1(1'b0), .out(sDesl[26]), .sel(or_1_out));
  Multiplexer multiplexer_188 (.in0(multiplexer_156_out), .in1(1'b0), .out(sDesl[27]), .sel(or_1_out));
  Multiplexer multiplexer_189 (.in0(multiplexer_157_out), .in1(1'b0), .out(sDesl[28]), .sel(or_1_out));
  Multiplexer multiplexer_190 (.in0(multiplexer_158_out), .in1(1'b0), .out(sDesl[29]), .sel(or_1_out));
  Multiplexer multiplexer_191 (.in0(multiplexer_159_out), .in1(1'b0), .out(sDesl[30]), .sel(or_1_out));
  Multiplexer multiplexer_192 (.in0(multiplexer_160_out), .in1(1'b0), .out(sDesl[31]), .sel(or_1_out));
  or or_1 (or_1_out, B[31], B[30], B[29], B[28], B[27], B[26], B[25], B[24], B[23], B[22], B[21], B[20], B[19], B[18], B[17], B[16], B[15], B[14], B[13], B[12], B[11], B[10], B[9], B[8], B[7], B[6], B[5]);

  // Other names for the same wires on the sheet: s0 = sDesl[0]; s1 = sDesl[1]; s2 = sDesl[2]; s3 = sDesl[3];
  //   s4 = sDesl[4]; s5 = sDesl[5]; s6 = sDesl[6]; s7 = sDesl[7]; s8 = sDesl[8]; s9 = sDesl[9]; s10 = sDesl[10];
  //   s11 = sDesl[11]; s12 = sDesl[12]; s13 = sDesl[13]; s14 = sDesl[14]; s15 = sDesl[15]; s16 = sDesl[16];
  //   s17 = sDesl[17]; s18 = sDesl[18]; s19 = sDesl[19]; s20 = sDesl[20]; s21 = sDesl[21]; s22 = sDesl[22];
  //   s23 = sDesl[23]; s24 = sDesl[24]; s25 = sDesl[25]; s26 = sDesl[26]; s27 = sDesl[27]; s28 = sDesl[28];
  //   s29 = sDesl[29]; s30 = sDesl[30]; s31 = sDesl[31]
endmodule

module extensinal (
  input  [15:0] E,
  output [31:0] out_2
);


  assign out_2 = {{17{E[15]}}, E[14:0]};
endmodule
